# Fritzing sketch Circuit Diagram (saved by Fritzing 0.9.3b)
breadboards: 2

parts:
  Part1 = Arduino BT
  S1 = H-Bridge with L298N
  BAT1 = 18650 battery holder [package=battery-18650-kit]
  BAT2 = 18650 battery holder [package=battery-18650-kit]
  BAT3 = 18650 battery holder [package=battery-18650-kit]
  M1 = DC Motor
  M2 = DC Motor
  M3 = DC Motor
  M4 = DC Motor
  Part2 = Bluetooth HC-05 Macho
  M5 = fc-51 [package=THT]
  M6 = fc-51 [package=THT]
  Part3 = Arduino Mega 2560 (Rev3)
  DI1 = 7-Segment LED Display [package=THT]
  tft1 = 3.2in tft touch screen
  Part4 = Thumb Joystick
  R1 = Resistor [tolerance=±5% resistance=220 package=THT]
  microSD1 = MicroSD Card Module
  SP1 = SPEAKER [package=pcb_mount_speaker]
  SP2 = SPEAKER [package=pcb_mount_speaker]
  R2 = Rotary Potentiometer (Small) [maximum_resistance=100kΩ package=THT]
  LED1 = LEDs [package=led10mm]
  LED2 = LEDs [package=led10mm]
  LED3 = LEDs [package=led10mm]
  LED4 = LEDs [package=led10mm]
  LED5 = LEDs [package=led10mm]
  R3 = Photocell (LDR) [package=THT]
  R4 = Resistor [tolerance=±5% resistance=220 package="0402 [SMD]"]
  SG1 = Buzzer 12mm [package=buzzer-ccv-kit]

nets:
  N1: Part1.D8, SG1.2
  N2: Part1.SCK/D13, LED5.C
  GND: Part1.GND, S1.GND, BAT3.-, Part2.GND, M5.pin2, M6.pin2, LED1.A, R4.Pin_1, SG1.1
  N3: Part1.A5, R4.Pin_0
  N4: Part1.RX/D0, Part2.TXD
  N5: Part1.TX/D1, Part2.RXD
  N6: Part1.D2, S1.IN1
  N7: Part1.PWM_D3, S1.IN2
  N8: Part1.D4, S1.IN3
  N9: Part1.PWM_D5, S1.IN4
  N10: Part1.PWM_D6, M6.pin1
  N11: Part1.RESET_WT11/D7, M5.pin1
  VIN: Part1.VIN, S1.5V
  N12: Part1.5V, M5.pin3, M6.pin3, R3.pin_0
  3V3: Part1.3V3, Part2.VCC
  N13: S1.12V, BAT1.+
  N14: S1.ENA, S1.ENA-5V
  N15: S1.ENB, S1.ENB-5V
  N16: S1.M1-01, M3.pin_2, M4.pin_2
  N17: S1.M1-02, M3.pin_1, M4.pin_1
  N18: S1.M2-01, M1.pin_2, M2.pin_2
  N19: S1.M2-02, M1.pin_1, M2.pin_1
  N20: BAT2.-, BAT3.+
  N21: Part3.A8, tft1.GND
  N22: Part3.A10, Part4.HORZ
  N23: Part3.A11, Part4.VERT
  N24: Part3.D16_PWM/TX2, tft1.NC#19
  N25: Part3.D15/RX3, tft1.NC#39
  GND_2: Part3.GND, Part4.GND, R1.Pin_1, microSD1.GND
  VCC: Part3.5V, Part4.VCC, microSD1.VCC, R2.leg1
  N26: Part3.D24, DI1.cathodeA
  N27: Part3.D25, DI1.cathodeB
  N28: Part3.D26, DI1.cathodeC
  N29: Part3.D27, DI1.cathodeDP
  N30: Part3.D28, DI1.cathodeG
  N31: Part3.D29, DI1.cathodeF
  N32: Part3.D30, DI1.cathodeE
  N33: Part3.D31, DI1.cathodeD
  N34: Part3.D46, SP1.-, SP2.-
  N35: Part3.D50, microSD1.MISO
  N36: Part3.D51, microSD1.MOSI
  N37: Part3.D52, microSD1.SCK
  N38: Part3.D53, microSD1.CS
  N39: DI1.commAnode#2, R1.Pin_0
  N40: SP1.+, SP2.+, R2.wiper
  N41: LED1.C, LED2.A
  N42: LED2.C, LED3.A
  N43: LED3.C, LED4.A
  N44: LED4.C, LED5.A

custom parts:
  H-Bridge with L298N: h-bridge
  18650 battery holder: 18650 Battery Holder
  3.2in tft touch screen: 3.2" tft touch screen lcd display
